// Logisim project 4 Bit Full Adder Circuit V4.circ as structural Verilog: 1 circuit, main circuit main
module main (
  input  A2,
  input  A1,
  input  A0,
  input  in_4,
  input  B2,
  input  B1,
  input  B0,
  input  in_8,
  output CARRY,
  output S3,
  output S2,
  output S1,
  output S0
);

  wire _02_out, A1_out, A2_out, A3_out, A4_out, A5_out, A6_out, A7_out, O1_out, X2_out, X4_out, X6_out;

  xor X1 (S0, in_4, in_8);
  and u_A1 (A1_out, in_4, in_8);
  xor X2 (X2_out, A0, A1_out);
  and u_A2 (A2_out, A0, A1_out);
  xor X3 (S1, X2_out, B0);
  and A3 (A3_out, X2_out, B0);
  or O1 (O1_out, A2_out, A3_out);
  xor X4 (X4_out, A1, O1_out);
  and A4 (A4_out, A1, O1_out);
  xor X5 (S2, X4_out, B1);
  and A5 (A5_out, X4_out, B1);
  or _02 (_02_out, A4_out, A5_out);
  xor X6 (X6_out, A2, _02_out);
  and A6 (A6_out, A2, _02_out);
  xor X7 (S3, X6_out, B2);
  and A7 (A7_out, X6_out, B2);
  or _03 (CARRY, A7_out, A6_out);

  // Notes on the sheet:
  //   A3
  //   B3
  //   S0
  //   CARRY
  //   CARRY
  //   S1
  //   CARRY
  //   CARRY
  //   S2
  //   CARRY
  //   CARRY
  //   S3
  //   CARRY
  //   FINAL CARRY
endmodule
